# Fritzing sketch Physik WPK Projekt (saved by Fritzing 0.9.3b)
breadboards: 1

parts:
  Part2 = RFID-RC522-v2
  Part1 = Arduino Uno (Rev3) - ICSP
  U1 = LCD-16X2 [package=lcd-16x2_noholes]
  R1 = TRIMPOT [package=trimpot_tc33]
  Bauteil1 = Arduino Leonardo (Rev3b)
  Keypad4x1 = Keypad Membran 4x4

nets:
  N1: Part2.SDA, Part1.D10_PWM/SS
  N2: Part2.SCK, Part1.D13/SCK
  N3: Part2.MOSI, Part1.D11_PWM/MOSI
  N4: Part2.MISO, Part1.D12/MISO
  GND: Part2.GND, Part1.GND, U1.VSS, U1.R_W, U1.A, U1.K, R1.WIPER, Bauteil1.GND
  N5: Part2.RST, Part1.D9_PWM
  N6: Part2.3_3V, Part1.3V3
  N7: Part1.A0, Bauteil1.D1/TX
  N8: Part1.D8, U1.DB7
  N9: Part1.D3_PWM, U1.RS
  N10: Part1.D4, U1.E
  N11: Part1.D5_PWM, U1.DB4
  N12: Part1.D6_PWM, U1.DB5
  N13: Part1.D7, U1.DB6
  N14: U1.VDD, R1.CCW
  N15: U1.VO, R1.CW
  N16: Bauteil1.D6_PWM/A7, Keypad4x1.Pin8
  N17: Bauteil1.D7, Keypad4x1.Pin7
  N18: Bauteil1.D8/A8, Keypad4x1.Pin6
  N19: Bauteil1.D9_PWM/A9, Keypad4x1.Pin5
  N20: Bauteil1.D10_PWM/A10, Keypad4x1.Pin4
  N21: Bauteil1.D11_PWM, Keypad4x1.Pin3
  N22: Bauteil1.D12/A11, Keypad4x1.Pin2
  N23: Bauteil1.D13_PWM, Keypad4x1.Pin1

custom parts:
  RFID-RC522-v2: A simple China made RFID-RC522 Reader; do check the pin labels, as this is a MFRC522 based clone.
  Keypad Membran 4x4: Membrane Keypad 4x4 Matrix
